# Fritzing sketch SolenoidSchematic (saved by Fritzing 0.9.3b)
breadboards: 1

parts:
  Q1 = pnp-Powertransistor [part_number="TIP 120" package="TO220 [THT]"]
  R1 = Resistor [tolerance=±5% resistance=2.2k package="2512 [SMD]"]
  Part1 = Arduino Uno (Rev3) - ICSP
  D1 = Rectifier Diode 10A [part_number=P1000K]
  R2 = Resistor [tolerance=±5% resistance=330 package="0603 [SMD]"]
  L1 = Solenoid

nets:
  N1: Q1.base, R1.Pin_1
  N2: Q1.collector, R2.Pin_1, L1.pin1
  N3: Q1.emitter, Part1.GND
  N4: R1.Pin_0, Part1.D11_PWM/MOSI
  N5: Part1.VIN, D1.cathode, L1.pin2
  N6: D1.anode, R2.Pin_0

notes:
  As resistências são de
  2.2KOhm (vermelho, vermelho, vermelho)
  e 330Ohm (laranja, laranja, castanho)

// code stored in the sketch: solenoid.ino
int beat[]={180,200,80,80,500};

void setup() {
  // put your setup code here, to run once:
  pinMode(11,OUTPUT);
}

void loop() {
  // put your main code here, to run repeatedly:´
  for (int c=0;c<5;c++) {
    digitalWrite(11,HIGH);
    delay(10);
    digitalWrite(11,LOW);
    delay(beat[c]);
  }
}

// code stored in the sketch: SolenoidSchematic.ino
int beat[]={180,200,80,80,500};

void setup() {
  // put your setup code here, to run once:
  pinMode(11,OUTPUT);
}

void loop() {
  // put your main code here, to run repeatedly:´
  for (int c=0;c<5;c++) {
    digitalWrite(11,HIGH);
    delay(10);
    digitalWrite(11,LOW);
    delay(beat[c]);
  }
}
